# Fritzing sketch Schematic (saved by Fritzing 0.9.10b)
breadboards: 1

parts:
  Part2 = Arduino Uno (Rev3) - ICSP  # not connected
  LED1 = LEDs [package=led10mm]
  R1 = Resistor [tolerance=±5% resistance=220 package="0603 [SMD]"]
  Mod1 = Passive Buzzer  # not connected

nets:
  N1: LED1.C, LED1.A, R1.Pin_1
